# Fritzing sketch IoT weather station (saved by Fritzing 0.9.3b)
breadboards: 1

parts:
  Arduino_Uno = Arduino Uno (Rev3)
  BMP180 = Barometric Pressure Sensor - BMP180 Breakout (GY-68)
  Water_Level_Sensor = Water Level Sensor
  NodeMCU_ESP8226 = NodeMCU V1.0
  MQ-135 = Gas Sensor Breakout Board
  R1-R3 = Resistor [tolerance=±5% resistance=330 package=THT]
  R1 = Resistor [tolerance=±5% resistance=330 package=THT]
  Level_shifter = Logic Level Converter
  DHT11 = DHT11 Humitidy and Temperature Sensor
  R4 = Resistor [tolerance=±5% resistance=10k package=THT]
  LED = RGB LED (com. cathode, rgb) [package="5 mm [THT]"]
  R2 = Resistor [tolerance=±5% resistance=330 package=THT]
  Part9 = FC-28 Soil Hygrometer Module - Probe
  Part10 = FC-28 Soil Hygrometer Module
  UV-sensor = GUVA-S12SD UV Light Sensor

nets (from the breadboard view):
  N1: Arduino_Uno.A0, UV-sensor.SIG
  N2: Arduino_Uno.A1, Water_Level_Sensor.SIG
  N3: Arduino_Uno.A2, Part10.AO
  N4: Arduino_Uno.A3, MQ-135.AOUT
  N5: Arduino_Uno.A4/SDA, BMP180.SDA
  N6: Arduino_Uno.A5/SCL, BMP180.SCL
  N7: Arduino_Uno.D2, Level_shifter.TX_HV
  N8: Arduino_Uno.D3_PWM, Level_shifter.RX_HV
  N9: Arduino_Uno.D4, DHT11.DATA, R4.Pin_0
  5V: Arduino_Uno.5V, BMP180.VCC, Water_Level_Sensor.VCC, MQ-135.5V, Level_shifter.HV, DHT11.VDD, R4.Pin_1, Part10.VCC, UV-sensor.5V
  GND: Arduino_Uno.GND, BMP180.GND, Water_Level_Sensor.GND, NodeMCU_ESP8226.GND, MQ-135.GND, Level_shifter.GND, DHT11.GND, LED.common_cathode, Part10.GND
  N10: NodeMCU_ESP8226.3V3, R1-R3.Pin_1, Level_shifter.LV
  N11: NodeMCU_ESP8226.D6, R1.Pin_1
  N12: NodeMCU_ESP8226.D7, R2.Pin_1
  N13: NodeMCU_ESP8226.RX, Level_shifter.TX_LV
  N14: NodeMCU_ESP8226.TX, Level_shifter.RX_LV
  N15: R1-R3.Pin_0, LED.red_anode
  N16: R1.Pin_0, LED.green_anode
  N17: LED.blue_anode, R2.Pin_0
  N18: Part9.POS, Part10.POS
  N19: Part9.NEG, Part10.NEG

notes:
  Ground on RGB is the longest leg

custom parts:
  Water Level Sensor: A water level sensor. This sensor operates at 3V to 5V. The Sig (signal) pin outputs an analogue signal that is in proportion to the amount of water in contact with the sensor.
  NodeMCU V1.0: ESP8266 based NodeMCU
  Gas Sensor Breakout Board: Gas sensor breakout board. Input voltage is 5V. Sensor output is available in analog and digital.
  DHT11 Humitidy and Temperature Sensor: DHT11 Humidity and Temperature Sensor
  FC-28 Soil Hygrometer Module - Probe: The FC-28 is a soil hygrometer module that uses the Texas Instruments LM393 comparator chip to provide an analog measurement of soil humidity.
  FC-28 Soil Hygrometer Module: The FC-28 is a soil hygrometer module that uses the Texas Instruments LM393 comparator chip to provide an analog measurement of soil humidity. The digital output is high when soil moisture is over a certain threshold, as determined by adjusting the potentiometer.
  GUVA-S12SD UV Light Sensor: Extend your light-sensing spectrum with this analog UV sensor module. It uses a UV photodiode, which can detect the 240-370nm range of light (which covers UVB and most of UVA spectrum). The signal level from the photodiode is very small, in the nano-ampere level, so we tossed on an opamp to amplify the signal to a more manageable volt-level.
